# Fritzing sketch IoT project schema (saved by Fritzing 0.9.3b)
breadboards: 2

parts:
  ESP32 = MH-ET LIVE ESP32 DEVKIT 38 pins
  HC-SR04_Sensor = HC-SR04 Ultrasonic Distance Sensor
  BAT = Battery block 9V
  Motor_Rechts = DC Motor
  IR_sensor_Array = 5-ir-array-sensor [package=THT]
  Motor_Links = DC Motor
  S1 = H-Bridge with L298N
  U1 = SWITCH-SPST-2 [package=r_sw_th]
  LED3 = smd LED [color="Red (633nm)" package="1206 [SMD]"]
  LED4 = smd LED [color="Red (633nm)" package="1206 [SMD]"]
  LED5 = smd LED [color="Red (633nm)" package="1206 [SMD]"]
  S2 = Pushbutton [package="[SMD]"]
  R1 = Resistor [tolerance=±5% resistance=220 package=THT]

nets:
  N1: ESP32.IO35, S1.ENB
  N2: ESP32.IO32, S1.IN4
  N3: ESP32.IO33, S1.IN3
  N4: ESP32.IO26, S1.IN2
  N5: ESP32.IO27, S1.IN1
  N6: ESP32.IO12, S1.ENA
  5V: ESP32.5V, ESP32.IO4, HC-SR04_Sensor.VCC, IR_sensor_Array.VCC, S1.5V, S2.Pin_3, S2.Pin_4
  GND: ESP32.GND, HC-SR04_Sensor.GND, BAT.-, IR_sensor_Array.GND, S1.GND, LED3.cathode, LED4.cathode, LED5.cathode, R1.Pin_0
  N7: ESP32.IO23, HC-SR04_Sensor.TRIG
  N8: ESP32.IO22, HC-SR04_Sensor.ECHO
  N9: ESP32.IO21, LED4.anode
  N10: ESP32.IO19, LED5.anode
  N11: ESP32.IO18, IR_sensor_Array.S1
  N12: ESP32.IO5, LED3.anode
  N13: ESP32.IO17, IR_sensor_Array.S3
  N14: ESP32.IO16, IR_sensor_Array.S5
  N15: BAT.+, U1.O
  N16: Motor_Rechts.pin_1, S1.M2-02, S1.ENA-5V
  N17: Motor_Rechts.pin_2, S1.M2-01
  N18: Motor_Links.pin_1, S1.M1-02
  N19: Motor_Links.pin_2, S1.M1-01
  N20: S1.12V, U1.P
  N21: S2.Pin_1, S2.Pin_2, R1.Pin_1

custom parts:
  MH-ET LIVE ESP32 DEVKIT 38 pins: http://mh.nodebb.com/topic/2/mh-et-live-esp32-devkit
  5-ir-array-sensor: 5 IR array sensor.
  H-Bridge with L298N: h-bridge
